# Fritzing sketch ElBanquos_1D_pong_mk1 (saved by Fritzing 0.9.3b)
breadboards: 1

parts:
  LED_RING = 12 NeoPixel Ring [part_number=1643]
  SP1 = SPEAKER [package=pcb_mount_speaker]
  R1 = Resistor [tolerance=±5% resistance=220 package=THT]
  Button_B = Pushbutton [package="[THT]"]
  Button_A = Pushbutton [package="[THT]"]
  The_uno = Arduino Uno (Rev3)

nets:
  N1: LED_RING.IN, The_uno.D12/MISO
  VDD: LED_RING.VDD, The_uno.5V
  GND: LED_RING.GND, R1.Pin_0, Button_B.Pin_1, Button_B.Pin_2, Button_A.Pin_1, Button_A.Pin_2, The_uno.GND
  N2: SP1.+, The_uno.D11_PWM/MOSI
  N3: SP1.-, R1.Pin_1
  N4: Button_B.Pin_3, Button_B.Pin_4, The_uno.D8
  N5: Button_A.Pin_3, Button_A.Pin_4, The_uno.D2

custom parts:
  12 NeoPixel Ring: 12 ultra bright smart LED NeoPixels are arranged in a circle with 1.5" (37mm) outer diameter. The rings are 'chainable' - connect the output pin of one to the input pin of another. Use only one microcontroller pin to control as many as you can chain together! Each LED is addressable as the driver chip is inside the LED. Each one has ~18mA constant current drive so the color will be very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
